// Logisim project p3.circ as structural Verilog: 1 circuit, main circuit main
module main (
  input  in_1,
  input  in_2,
  input  in_3,
  input  in_4,
  input  in_5
);

  wire adder_2_cout, CLCK, CTRLW, decoder_1_out0, decoder_1_out1, decoder_1_out2, decoder_1_out3,
       decoder_1_out4, decoder_1_out5, decoder_1_out6, decoder_1_out7, undriven;
  wire [2:0] adder_5_out, adder_6_out, SELB, SELD, SELR;
  wire [7:0] adder_1_out, register_1_q;
  wire [11:0] ALU;
  wire [15:0] A, ADD, adder_8_out, AUR, B, C, D, DOT, DOTA, INSRT, LIR, multiplexer_8_out, multiplier_1_out,
       multiplier_2_out, multiplier_3_out, multiplier_4_out, R0_q, R1_q, R2_q, R3_q, R4_q, R5_q, R6_q, R7_q,
       RD;
  wire [15:12] rom_1_data;

  Register register_1 (.D(adder_1_out), .en(1'b1), .clk(CLCK), .Q(register_1_q), .clr(in_4));
  Clock clock_1 (.out(CLCK));
  // Probe on register_1_q
  ROM #(.dataWidth(16)) rom_1 (.addr(register_1_q), .data({rom_1_data, ALU[7:0], SELR, CTRLW}));
  Adder adder_1 (.a(register_1_q), .b(8'h1), .out(adder_1_out));  // open: cin, cout
  // Probe on adder_1_out
  // Probe on SELR
  Decoder #(.enable("false"), .select(3)) decoder_1 (
    .out0(decoder_1_out0), .out1(decoder_1_out1), .out2(decoder_1_out2), .out3(decoder_1_out3),
    .out4(decoder_1_out4), .out5(decoder_1_out5), .out6(decoder_1_out6), .out7(decoder_1_out7), .sel(SELR));
  Register #(.width(16)) R7 (.D(INSRT), .en(decoder_1_out7), .clk(CLCK), .Q(R7_q), .clr(in_2));
  Register #(.width(16)) R6 (.D(INSRT), .en(decoder_1_out6), .clk(CLCK), .Q(R6_q), .clr(in_2));
  Register #(.width(16)) R5 (.D(INSRT), .en(decoder_1_out5), .clk(CLCK), .Q(R5_q), .clr(in_2));
  Register #(.width(16)) R4 (.D(INSRT), .en(decoder_1_out4), .clk(CLCK), .Q(R4_q), .clr(in_2));
  Multiplexer #(.width(16)) multiplexer_1 (.in0(AUR), .in1(LIR), .out(INSRT), .sel(CTRLW));
  Multiplexer #(.select(3), .width(16)) multiplexer_2 (
    .in0(R0_q), .in1(R1_q), .in2(R2_q), .in3(R3_q), .in4(R4_q), .in5(R5_q), .in6(R6_q), .in7(R7_q), .out(RD),
    .sel(SELR));
  Register #(.width(16)) R3 (.D(INSRT), .en(decoder_1_out3), .clk(CLCK), .Q(R3_q), .clr(in_2));
  Register #(.width(16)) R2 (.D(INSRT), .en(decoder_1_out2), .clk(CLCK), .Q(R2_q), .clr(in_2));
  Multiplexer #(.select(3), .width(16)) multiplexer_3 (
    .in0(R0_q), .in1(R1_q), .in2(R2_q), .in3(R3_q), .in4(R4_q), .in5(R5_q), .in6(R6_q), .in7(R7_q), .out(A),
    .sel(ALU[4:2]));
  Register #(.width(16)) R1 (.D(INSRT), .en(decoder_1_out1), .clk(CLCK), .Q(R1_q), .clr(in_2));
  Multiplexer #(.select(3), .width(16)) multiplexer_4 (
    .in0(R0_q), .in1(R1_q), .in2(R2_q), .in3(R3_q), .in4(R4_q), .in5(R5_q), .in6(R6_q), .in7(R7_q), .out(B),
    .sel(SELB));
  assign LIR = {{4{ALU[11]}}, ALU};  // Bit_Extender bit_extender_1
  Register #(.width(16)) R0 (.D(INSRT), .en(decoder_1_out0), .clk(CLCK), .Q(R0_q), .clr(in_2));
  Multiplexer #(.select(3), .width(16)) multiplexer_5 (
    .in0(R0_q), .in1(R1_q), .in2(R2_q), .in3(R3_q), .in4(R4_q), .in5(R5_q), .in6(R6_q), .in7(R7_q), .out(C),
    .sel(ALU[7:5]));
  Multiplexer #(.select(3), .width(16)) multiplexer_6 (
    .in0(R0_q), .in1(R1_q), .in2(R2_q), .in3(R3_q), .in4(R4_q), .in5(R5_q), .in6(R6_q), .in7(R7_q), .out(D),
    .sel(SELD));
  Multiplexer #(.width(16)) multiplexer_7 (.in0(ADD), .in1(multiplexer_8_out), .out(AUR), .sel(ALU[1]));
  Multiplexer #(.width(16)) multiplexer_8 (.in0(DOT), .in1(DOTA), .out(multiplexer_8_out), .sel(ALU[0]));
  // Probe on RD
  Adder #(.width(16)) adder_2 (.a(RD), .b(A), .out(ADD), .cin(in_3), .cout(adder_2_cout));
  Adder #(.width(3)) adder_3 (.a(SELR), .b(3'b001), .out(SELB), .cin(undriven));  // open: cout
  Adder #(.width(3)) adder_4 (.a(ALU[4:2]), .b(3'b001), .out(SELD), .cin(undriven));  // open: cout
  Adder #(.width(3)) adder_5 (.a(ALU[4:2]), .b(3'b001), .out(adder_5_out), .cin(in_5));  // open: cout
  Adder #(.width(3)) adder_6 (.a(ALU[7:5]), .b(3'b001), .out(adder_6_out), .cin(in_5));  // open: cout
  // Probe on adder_2_cout
  Multiplier #(.width(16)) multiplier_1 (.a(RD), .b(A), .out(multiplier_1_out));  // open: cin, cout
  Multiplier #(.mode("twosComplement"), .width(16)) multiplier_2 (
    .a(B), .b(D), .out(multiplier_2_out));  // open: cin, cout
  Multiplier #(.width(16)) multiplier_3 (.a(A), .b(C), .out(multiplier_3_out));  // open: cin, cout
  Multiplier #(.mode("twosComplement"), .width(16)) multiplier_4 (
    .a(B), .b(D), .out(multiplier_4_out));  // open: cin, cout
  Adder #(.width(16)) adder_7 (.a(multiplier_1_out), .b(multiplier_2_out), .out(DOT));  // open: cin, cout
  Adder #(.width(16)) adder_8 (.a(multiplier_3_out), .b(multiplier_4_out), .out(adder_8_out));  // open: cin, cout
  Adder #(.width(16)) adder_9 (.a(RD), .b(adder_8_out), .out(DOTA));  // open: cin, cout

  // Other names for the same wires on the sheet: AU[11:0] = ALU; FUNC2[1:0] = ALU[1:0]; LI[11:0] = ALU;
  //   SELA[2:0] = ALU[4:2]; SELC[2:0] = ALU[7:5]; SELRD[2:0] = SELR

  // Notes on the sheet:
  //   contents of rom_1 (hex, n*v repeats v):
  //   1d34 1234 aaaa 100
endmodule
